# Fritzing sketch actuator-led (saved by Fritzing 0.9.3b)
breadboards: 1

parts:
  U1 = NodeMCU V1.0
  R3 = Resistor [tolerance=±5% resistance=330 package="2512 [SMD]"]
  LED1 = smd LED [color="Green (555nm)" package="0603 [SMD]"]

nets:
  N1: U1.D0, LED1.anode
  N2: U1.GND, R3.Pin_1
  N3: R3.Pin_0, LED1.cathode

custom parts:
  NodeMCU V1.0: ESP8266 based NodeMCU
