# Fritzing sketch actuator-relay (saved by Fritzing 0.9.3b)
breadboards: 1

parts:
  U1 = NodeMCU V1.0
  LED3 = LEDs [package=led10mm]
  KY-2 = Keyes Relay [package=THT]

nets:
  N1: U1.D0, KY-2.ground
  N2: U1.3V3, KY-2.signal
  N3: U1.GND, KY-2.power
  N4: LED3.C, KY-2.NO

notes:
  10A 110/220V AC

custom parts:
  NodeMCU V1.0: ESP8266 based NodeMCU
  LEDs: LEDs Standard schematic elements and footprints for 5mm, 3mm, 1206, and 0603 sized LEDs. 5mm - Spark Fun Electronics SKU : COM-00529 (and others)
  Keyes Relay: The Keyes 5V relay module is suitable for SCM development, home appliance control. It uses a 5V~12V TIL control signal which can control DC / AC signal.
