# Fritzing sketch actuator-rgb-led (saved by Fritzing 0.9.3b)
breadboards: 1

parts:
  R1 = Resistor [tolerance=±5% resistance=330 package="0402 [SMD]"]
  R2 = Resistor [tolerance=±5% resistance=330 package="0402 [SMD]"]
  R3 = Resistor [tolerance=±5% resistance=330 package="0402 [SMD]"]
  U1 = NodeMCU V1.0
  LED1 = RGB LED (com. cathode, rgb) [package="5 mm [THT]"]

nets:
  N1: R1.Pin_0, LED1.red_anode
  N2: R1.Pin_1, U1.D0
  N3: R2.Pin_0, LED1.green_anode
  N4: R2.Pin_1, U1.D1
  N5: R3.Pin_0, LED1.blue_anode
  N6: R3.Pin_1, U1.D2
  N7: U1.GND, LED1.common_cathode

custom parts:
  NodeMCU V1.0: ESP8266 based NodeMCU
