# Fritzing sketch fs-circuit (saved by Fritzing 0.9.3b)
breadboards: 1

parts:
  LED1 = RGB LED (com. cathode, rbg) [package="5 mm [THT]"]
  R1 = Resistor [tolerance=±5% resistance=330 package="0402 [SMD]"]
  R2 = Resistor [tolerance=±5% resistance=330 package="0402 [SMD]"]
  R3 = Resistor [tolerance=±5% resistance=330 package="0402 [SMD]"]
  SW-1 = Vibration sensor module
  U1 = NodeMCU V1.0

nets:
  N1: LED1.red_anode, R1.Pin_0
  N2: LED1.common_cathode, SW-1.Ground, U1.GND
  N3: LED1.blue_anode, R2.Pin_0
  N4: LED1.green_anode, R3.Pin_0
  N5: R1.Pin_1, U1.D5
  N6: R2.Pin_1, U1.D6
  N7: R3.Pin_1, U1.D7
  VCC: SW-1.vcc, U1.3V3
  N8: SW-1.Digital_output, U1.D0

custom parts:
  Vibration sensor module: Single-roller type full induction trigger switch. When no vibration or tilt, the product is ON conduction state, and in the steady state, when a vibration or tilt, the switch will be rendered instantly disconnect the conductive resistance increases, generating a current pulse signal, thereby triggering circuit. The default state of the swith is close Digital output Supply voltage:3.3V-5V On-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
  NodeMCU V1.0: ESP8266 based NodeMCU
