# Fritzing sketch sensor-capacitive-touch-button-ttp223 (saved by Fritzing 0.9.3b)
breadboards: 1

parts:
  U1 = NodeMCU V1.0
  TTP223B2 = TTP223B Capacitive Touch Sensor Module

nets:
  N1: U1.D0, TTP223B2.SIG
  3V3: U1.3V3, TTP223B2.VCC
  GND: U1.GND, TTP223B2.GND

custom parts:
  NodeMCU V1.0: ESP8266 based NodeMCU
  TTP223B Capacitive Touch Sensor Module: The TTP223B capacitive touch sensor module uses the TTP223B IC. The appropriate voltage is approximately 2 to 5.5 volts.
