# Fritzing sketch sensor-digital-luminosity-ldr (saved by Fritzing 0.9.3b)
breadboards: 1

parts:
  U1 = NodeMCU V1.0
  SW-2 = Vibration sensor module

nets:
  N1: U1.D0, SW-2.Digital_output
  3V3: U1.3V3, SW-2.vcc
  N2: U1.GND, SW-2.Ground

custom parts:
  NodeMCU V1.0: ESP8266 based NodeMCU
  Vibration sensor module: Single-roller type full induction trigger switch. When no vibration or tilt, the product is ON conduction state, and in the steady state, when a vibration or tilt, the switch will be rendered instantly disconnect the conductive resistance increases, generating a current pulse signal, thereby triggering circuit. The default state of the swith is close Digital output Supply voltage:3.3V-5V On-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
