# Fritzing sketch sensor-humidity-and-temperature-dht11 (saved by Fritzing 0.9.3b)
breadboards: 1

parts:
  R1 = Resistor [tolerance=±5% resistance=10k package="0402 [SMD]"]
  U1 = NodeMCU V1.0
  DHT1 = DHT11 Humitidy and Temperature Sensor

nets:
  N1: R1.Pin_0, U1.D0, DHT1.DATA
  3V3: R1.Pin_1, U1.3V3, DHT1.VDD
  GND: U1.GND, DHT1.GND

custom parts:
  NodeMCU V1.0: ESP8266 based NodeMCU
  DHT11 Humitidy and Temperature Sensor: DHT11 Humidity and Temperature Sensor
