# Fritzing sketch sensor-luminosity-ldr (saved by Fritzing 0.9.3b)
breadboards: 1

parts:
  U1 = NodeMCU V1.0
  R3 = Resistor [tolerance=±5% resistance=10k package="2512 [SMD]"]
  R2 = Photocell (LDR) [package=THT]

nets:
  N1: U1.3V3, R2.pin_0
  N2: U1.GND, R3.Pin_1
  N3: U1.A0, R3.Pin_0, R2.pin_1

custom parts:
  NodeMCU V1.0: ESP8266 based NodeMCU
