# Fritzing sketch sensor-reflexive-obstacle-FC-51 (saved by Fritzing 0.9.3b)
breadboards: 1

parts:
  U1 = NodeMCU V1.0
  M1 = fc-51 [package=THT]

nets:
  N1: U1.D0, M1.pin1
  N2: U1.3V3, M1.pin3
  N3: U1.GND, M1.pin2

custom parts:
  NodeMCU V1.0: ESP8266 based NodeMCU
