# Fritzing sketch sensor-tilt-sw-200d (saved by Fritzing 0.9.3b)
breadboards: 1

parts:
  U1 = NodeMCU V1.0
  R3 = Resistor [tolerance=±5% resistance=10k package="2512 [SMD]"]
  S2 = TILT-SWITCH-SW-200D [package=reed_switch_plastic]

nets:
  N1: U1.D0, R3.Pin_0, S2.2
  N2: U1.3V3, S2.1
  N3: U1.GND, R3.Pin_1

custom parts:
  NodeMCU V1.0: ESP8266 based NodeMCU
