# Fritzing sketch sensor-ultrasonic-distance-hc-sr04 (saved by Fritzing 0.9.3b)
breadboards: 1

parts:
  U1 = NodeMCU V1.0
  hc-sr1 = hc-sr04

nets:
  N1: U1.D0, hc-sr1.Trig
  N2: U1.D1, hc-sr1.Echo
  3V3: U1.3V3, hc-sr1.VCC
  GND: U1.GND, hc-sr1.GND

custom parts:
  NodeMCU V1.0: ESP8266 based NodeMCU
